// Logisim project adh0.circ as structural Verilog
module ALU (
  input  [2:0] op,
  input  [7:0] x,
  input  [7:0] y,
  output [7:0] Z
);

  wire n7404_1_pin8, n7404_1_pin10, n7404_1_pin12, n7421_1_pin6, n7432_2_pin8, n7442_1_pin1, n7442_1_pin2,
       n7442_1_pin3, n7442_1_pin4, n7442_1_pin5, n7442_1_pin6, n7442_1_pin7, n7442_1_pin9, n7442_1_pin12,
       n7486_1_pin2, n74283_1_pin7;
  wire [7:0] adders_pin4, ands_pin6, n7404_2_pin2, n7432_1_pin3, n7486_1_pin11, n7486_2_pin3;

  _7442 u_7442_1 (
    .pin1(n7442_1_pin1), .pin2(n7442_1_pin2), .pin3(n7442_1_pin3), .pin4(n7442_1_pin4), .pin5(n7442_1_pin5),
    .pin6(n7442_1_pin6), .pin7(n7442_1_pin7), .pin15(op[0]), .pin14(op[1]), .pin13(op[2]),
    .pin12(n7442_1_pin12), .pin9(n7442_1_pin9));  // open: pin11, pin10
  _7404 u_7404_1 (
    .pin13(n7442_1_pin2), .pin12(n7404_1_pin12), .pin11(n7442_1_pin3), .pin10(n7404_1_pin10),
    .pin9(n7442_1_pin4), .pin8(n7404_1_pin8));  // open: pin1, pin2, pin3, pin4, pin5, pin6
  _7408 u_7408_1 (
    .pin1(y[5]), .pin2(x[5]), .pin3(ands_pin6[5]), .pin4(y[4]), .pin5(x[4]), .pin6(ands_pin6[4]),
    .pin13(y[7]), .pin12(x[7]), .pin11(ands_pin6[7]), .pin10(y[6]), .pin9(x[6]), .pin8(ands_pin6[6]));
  _7432 u_7432_1 (
    .pin1(x[0]), .pin2(y[0]), .pin3(n7432_1_pin3[0]), .pin4(x[1]), .pin5(y[1]), .pin6(n7432_1_pin3[1]),
    .pin13(x[7]), .pin12(y[7]), .pin11(n7432_1_pin3[7]), .pin10(x[6]), .pin9(y[6]), .pin8(n7432_1_pin3[6]));
  _7486 u_7486_1 (
    .pin1(y[4]), .pin2(n7486_1_pin2), .pin3(n7486_1_pin11[4]), .pin4(y[5]), .pin5(n7486_1_pin2),
    .pin6(n7486_1_pin11[5]), .pin13(y[0]), .pin12(n7486_1_pin2), .pin11(n7486_1_pin11[0]), .pin10(y[1]),
    .pin9(n7486_1_pin2), .pin8(n7486_1_pin11[1]));
  _7432 u_7432_2 (
    .pin13(n7404_1_pin8), .pin12(n7404_1_pin10), .pin11(n7486_1_pin2), .pin10(n7404_1_pin10),
    .pin9(n7404_1_pin12), .pin8(n7432_2_pin8));  // open: pin1, pin2, pin3, pin4, pin5, pin6
  _7408 ands (
    .pin1(y[1]), .pin2(x[1]), .pin3(ands_pin6[1]), .pin4(y[0]), .pin5(x[0]), .pin6(ands_pin6[0]),
    .pin13(y[3]), .pin12(x[3]), .pin11(ands_pin6[3]), .pin10(y[2]), .pin9(x[2]), .pin8(ands_pin6[2]));
  _7432 ors (
    .pin1(x[4]), .pin2(y[4]), .pin3(n7432_1_pin3[4]), .pin4(x[5]), .pin5(y[5]), .pin6(n7432_1_pin3[5]),
    .pin13(x[3]), .pin12(y[3]), .pin11(n7432_1_pin3[3]), .pin10(x[2]), .pin9(y[2]), .pin8(n7432_1_pin3[2]));
  _7486 inv (
    .pin1(y[6]), .pin2(n7486_1_pin2), .pin3(n7486_1_pin11[6]), .pin4(y[7]), .pin5(n7486_1_pin2),
    .pin6(n7486_1_pin11[7]), .pin13(y[2]), .pin12(n7486_1_pin2), .pin11(n7486_1_pin11[2]), .pin10(y[3]),
    .pin9(n7486_1_pin2), .pin8(n7486_1_pin11[3]));
  _7421 u_7421_1 (
    .pin1(n7442_1_pin1), .pin2(n7442_1_pin2), .pin4(n7442_1_pin3), .pin5(n7442_1_pin4), .pin6(n7421_1_pin6));  // open: pin3, pin13, pin12, pin11, pin10, pin9, pin8
  _7404 u_7404_2 (
    .pin1(x[0]), .pin2(n7404_2_pin2[0]), .pin3(x[1]), .pin4(n7404_2_pin2[1]), .pin5(x[4]),
    .pin6(n7404_2_pin2[4]), .pin13(x[7]), .pin12(n7404_2_pin2[7]), .pin11(x[6]), .pin10(n7404_2_pin2[6]));  // open: pin9, pin8
  _7486 u_7486_2 (
    .pin1(x[0]), .pin2(y[0]), .pin3(n7486_2_pin3[0]), .pin4(x[1]), .pin5(y[1]), .pin6(n7486_2_pin3[1]),
    .pin13(x[7]), .pin12(y[7]), .pin11(n7486_2_pin3[7]), .pin10(x[6]), .pin9(y[6]), .pin8(n7486_2_pin3[6]));
  _74283 u_74283_1 (
    .pin1(adders_pin4[5]), .pin2(n7486_1_pin11[5]), .pin3(x[5]), .pin4(adders_pin4[4]), .pin5(x[4]),
    .pin6(n7486_1_pin11[4]), .pin7(n74283_1_pin7), .pin15(n7486_1_pin11[6]), .pin14(x[6]),
    .pin13(adders_pin4[6]), .pin12(x[7]), .pin11(n7486_1_pin11[7]), .pin10(adders_pin4[7]));  // open: pin9
  _7404 invs (
    .pin3(x[5]), .pin4(n7404_2_pin2[5]), .pin13(x[3]), .pin12(n7404_2_pin2[3]), .pin11(x[2]),
    .pin10(n7404_2_pin2[2]));  // open: pin1, pin2, pin5, pin6, pin9, pin8
  _7486 xors (
    .pin1(x[4]), .pin2(y[4]), .pin3(n7486_2_pin3[4]), .pin4(x[5]), .pin5(y[5]), .pin6(n7486_2_pin3[5]),
    .pin13(x[3]), .pin12(y[3]), .pin11(n7486_2_pin3[3]), .pin10(x[2]), .pin9(y[2]), .pin8(n7486_2_pin3[2]));
  _74283 adders (
    .pin1(adders_pin4[1]), .pin2(n7486_1_pin11[1]), .pin3(x[1]), .pin4(adders_pin4[0]), .pin5(x[0]),
    .pin6(n7486_1_pin11[0]), .pin7(n7432_2_pin8), .pin15(n7486_1_pin11[2]), .pin14(x[2]),
    .pin13(adders_pin4[2]), .pin12(x[3]), .pin11(n7486_1_pin11[3]), .pin10(adders_pin4[3]),
    .pin9(n74283_1_pin7));
  _74244 trans2 (
    .pin1(n7442_1_pin7), .pin2(n7404_2_pin2[0]), .pin3(Z[7]), .pin4(n7404_2_pin2[1]), .pin5(Z[6]),
    .pin6(n7404_2_pin2[4]), .pin7(Z[3]), .pin8(n7404_2_pin2[5]), .pin9(Z[2]), .pin19(n7442_1_pin7),
    .pin18(Z[0]), .pin17(n7404_2_pin2[7]), .pin16(Z[1]), .pin15(n7404_2_pin2[6]), .pin14(Z[4]),
    .pin13(n7404_2_pin2[3]), .pin12(Z[5]), .pin11(n7404_2_pin2[2]));
  _74244 trans0 (
    .pin1(n7421_1_pin6), .pin2(adders_pin4[0]), .pin3(Z[7]), .pin4(adders_pin4[1]), .pin5(Z[6]),
    .pin6(adders_pin4[4]), .pin7(Z[3]), .pin8(adders_pin4[5]), .pin9(Z[2]), .pin19(n7421_1_pin6),
    .pin18(Z[0]), .pin17(adders_pin4[7]), .pin16(Z[1]), .pin15(adders_pin4[6]), .pin14(Z[4]),
    .pin13(adders_pin4[3]), .pin12(Z[5]), .pin11(adders_pin4[2]));
  _74244 trans3 (
    .pin1(n7442_1_pin9), .pin2(n7486_2_pin3[0]), .pin3(Z[7]), .pin4(n7486_2_pin3[1]), .pin5(Z[6]),
    .pin6(n7486_2_pin3[4]), .pin7(Z[3]), .pin8(n7486_2_pin3[5]), .pin9(Z[2]), .pin19(n7442_1_pin9),
    .pin18(Z[0]), .pin17(n7486_2_pin3[7]), .pin16(Z[1]), .pin15(n7486_2_pin3[6]), .pin14(Z[4]),
    .pin13(n7486_2_pin3[3]), .pin12(Z[5]), .pin11(n7486_2_pin3[2]));
  _74244 trans1 (
    .pin1(n7442_1_pin5), .pin2(n7432_1_pin3[0]), .pin3(Z[7]), .pin4(n7432_1_pin3[1]), .pin5(Z[6]),
    .pin6(n7432_1_pin3[4]), .pin7(Z[3]), .pin8(n7432_1_pin3[5]), .pin9(Z[2]), .pin19(n7442_1_pin5),
    .pin18(Z[0]), .pin17(n7432_1_pin3[7]), .pin16(Z[1]), .pin15(n7432_1_pin3[6]), .pin14(Z[4]),
    .pin13(n7432_1_pin3[3]), .pin12(Z[5]), .pin11(n7432_1_pin3[2]));
  _74244 trans4 (
    .pin1(n7442_1_pin6), .pin2(ands_pin6[0]), .pin3(Z[7]), .pin4(ands_pin6[1]), .pin5(Z[6]),
    .pin6(ands_pin6[4]), .pin7(Z[3]), .pin8(ands_pin6[5]), .pin9(Z[2]), .pin19(n7442_1_pin6), .pin18(Z[0]),
    .pin17(ands_pin6[7]), .pin16(Z[1]), .pin15(ands_pin6[6]), .pin14(Z[4]), .pin13(ands_pin6[3]),
    .pin12(Z[5]), .pin11(ands_pin6[2]));
  // also tied to GND on the sheet: n7442_1_pin12
endmodule

module AT28C64B (
  input  A0,
  input  A1,
  input  A2,
  input  A3,
  input  A4,
  input  A5,
  input  A6,
  input  A7,
  input  A8,
  input  A9,
  input  A10,
  input  A11,
  input  A12,
  input  CE_N,
  input  WE_N,
  input  OE_N,
  input  I0,
  input  I1,
  input  I2,
  input  I3,
  input  I4,
  input  I5,
  input  I6,
  input  I7,
  output O0,
  output O1,
  output O2,
  output O3,
  output O4,
  output O5,
  output O6,
  output O7
);

  wire nor_1_out, nor_2_out, not_1_out;
  wire [7:0] ram_1_dout;
  wire [12:0] controlled_buffer_1_out;

  nor nor_1 (nor_1_out, CE_N, WE_N);
  not not_1 (not_1_out, CE_N);
  nor nor_2 (nor_2_out, CE_N, OE_N);
  assign controlled_buffer_1_out = not_1_out ? {A12, A11, A10, A9, A8, A7, A6, A5, A4, A3, A2, A1, A0} : 13'bz;  // Controlled_Buffer controlled_buffer_1
  RAM #(.addrWidth(13), .trigger("high")) ram_1 (
    .addr(controlled_buffer_1_out), .we(nor_1_out), .oe(nor_2_out), .din({I7, I6, I5, I4, I3, I2, I1, I0}),
    .dout(ram_1_dout));
  assign {O7, O6, O5, O4, O3, O2, O1, O0} = nor_2_out ? ram_1_dout : 8'bz;  // Controlled_Buffer controlled_buffer_2
endmodule
